// Logisim project modular-sap-logisim.circ as structural Verilog: 5 circuits, main circuit main
module main (
  input  in_1,
  input  in_2,
  input  in_3,
  input  in_4,
  input  in_5,
  input  in_6,
  input  in_7,
  input  in_8,
  input  in_9,
  output out_10,
  output out_11,
  output out_12,
  output out_13,
  output out_14,
  output out_15,
  output out_16,
  output out_17
);

  wire clock_1_out;

  gp_reg gp_reg_1 (
    .out_11(out_10), .out_12(out_11), .out_13(out_12), .out_14(out_13), .out_15(out_14), .out_16(out_15),
    .out_17(out_16), .out_18(out_17), .in_1(in_1), .in_2(in_2), .in_3(in_3), .in_4(in_4), .in_5(in_5),
    .in_6(in_6), .in_7(in_7), .in_8(in_8), .in_9(clock_1_out), .in_10(in_9));
  Clock clock_1 (.out(clock_1_out));
endmodule

module gp_reg (
  input  in_1,
  input  in_2,
  input  in_3,
  input  in_4,
  input  in_5,
  input  in_6,
  input  in_7,
  input  in_8,
  input  in_9,
  input  in_10,
  output out_11,
  output out_12,
  output out_13,
  output out_14,
  output out_15,
  output out_16,
  output out_17,
  output out_18
);

  wire multiplexer_1_out, multiplexer_2_out, multiplexer_3_out, multiplexer_4_out, multiplexer_5_out,
       multiplexer_6_out, multiplexer_7_out, multiplexer_8_out, not_1_out;

  not not_1 (not_1_out, in_10);
  Multiplexer #(.enable("false")) multiplexer_1 (.in0(in_1), .in1(out_11), .out(multiplexer_1_out), .sel(not_1_out));
  D_Flip_Flop d_ff_1 (.clk(in_9), .D(multiplexer_1_out), .Q(out_11));  // open: Qn, preset, reset
  Multiplexer #(.enable("false")) multiplexer_2 (.in0(in_2), .in1(out_12), .out(multiplexer_2_out), .sel(not_1_out));
  D_Flip_Flop d_ff_2 (.clk(in_9), .D(multiplexer_2_out), .Q(out_12));  // open: Qn, preset, reset
  Multiplexer #(.enable("false")) multiplexer_3 (.in0(in_3), .in1(out_13), .out(multiplexer_3_out), .sel(not_1_out));
  Multiplexer #(.enable("false")) multiplexer_4 (.in0(in_4), .in1(out_14), .out(multiplexer_4_out), .sel(not_1_out));
  D_Flip_Flop d_ff_3 (.clk(in_9), .D(multiplexer_3_out), .Q(out_13));  // open: Qn, preset, reset
  D_Flip_Flop d_ff_4 (.clk(in_9), .D(multiplexer_4_out), .Q(out_14));  // open: Qn, preset, reset
  Multiplexer #(.enable("false")) multiplexer_5 (.in0(in_5), .in1(out_15), .out(multiplexer_5_out), .sel(not_1_out));
  Multiplexer #(.enable("false")) multiplexer_6 (.in0(in_6), .in1(out_16), .out(multiplexer_6_out), .sel(not_1_out));
  D_Flip_Flop d_ff_5 (.clk(in_9), .D(multiplexer_5_out), .Q(out_15));  // open: Qn, preset, reset
  D_Flip_Flop d_ff_6 (.clk(in_9), .D(multiplexer_6_out), .Q(out_16));  // open: Qn, preset, reset
  Multiplexer #(.enable("false")) multiplexer_7 (.in0(in_7), .in1(out_17), .out(multiplexer_7_out), .sel(not_1_out));
  D_Flip_Flop d_ff_7 (.clk(in_9), .D(multiplexer_7_out), .Q(out_17));  // open: Qn, preset, reset
  Multiplexer #(.enable("false")) multiplexer_8 (.in0(in_8), .in1(out_18), .out(multiplexer_8_out), .sel(not_1_out));
  D_Flip_Flop d_ff_8 (.clk(in_9), .D(multiplexer_8_out), .Q(out_18));  // open: Qn, preset, reset
endmodule

module full_adder (
  input  in_1,
  input  in_2,
  input  in_3,
  output out_4,
  output out_5
);

  wire and_1_out, and_2_out, xor_1_out;

  and and_1 (and_1_out, in_1, in_2);
  xor xor_1 (xor_1_out, in_1, in_2);
  and and_2 (and_2_out, xor_1_out, in_3);
  xor xor_2 (out_4, xor_1_out, in_3);
  or or_1 (out_5, and_1_out, and_2_out);
endmodule

module ripple_carry_adder (
  input  in_1,
  input  in_2,
  input  in_3,
  input  in_4,
  input  in_5,
  input  in_6,
  input  in_7,
  input  in_8,
  input  in_9,
  input  in_10,
  input  in_11,
  input  in_12,
  input  in_13,
  input  in_14,
  input  in_15,
  input  in_16,
  input  in_17,
  output out_18,
  output out_19,
  output out_20,
  output out_21,
  output out_22,
  output out_23,
  output out_24,
  output out_25,
  output out_26
);

  wire full_adder_1_out_5, full_adder_2_out_5, full_adder_3_out_5, full_adder_4_out_5, full_adder_5_out_5,
       full_adder_6_out_5, full_adder_7_out_5;

  full_adder full_adder_1 (.out_4(out_18), .out_5(full_adder_1_out_5), .in_1(in_1), .in_2(in_2), .in_3(in_3));
  full_adder full_adder_2 (
    .out_4(out_19), .out_5(full_adder_2_out_5), .in_1(in_4), .in_2(in_5), .in_3(full_adder_1_out_5));
  full_adder full_adder_3 (
    .out_4(out_20), .out_5(full_adder_3_out_5), .in_1(in_6), .in_2(in_7), .in_3(full_adder_2_out_5));
  full_adder full_adder_4 (
    .out_4(out_21), .out_5(full_adder_4_out_5), .in_1(in_8), .in_2(in_9), .in_3(full_adder_3_out_5));
  full_adder full_adder_5 (
    .out_4(out_22), .out_5(full_adder_5_out_5), .in_1(in_10), .in_2(in_11), .in_3(full_adder_4_out_5));
  full_adder full_adder_6 (
    .out_4(out_23), .out_5(full_adder_6_out_5), .in_1(in_12), .in_2(in_13), .in_3(full_adder_5_out_5));
  full_adder full_adder_7 (
    .out_4(out_24), .out_5(full_adder_7_out_5), .in_1(in_14), .in_2(in_15), .in_3(full_adder_6_out_5));
  full_adder full_adder_8 (.out_4(out_25), .out_5(out_26), .in_1(in_16), .in_2(in_17), .in_3(full_adder_7_out_5));
endmodule

module arithmatic_unit (
  input  in_1,
  input  in_2,
  input  in_3,
  input  in_4,
  input  in_5,
  input  in_6,
  input  in_7,
  input  in_8,
  input  in_9,
  input  in_10,
  input  in_11,
  input  in_12,
  input  in_13,
  input  in_14,
  input  in_15,
  input  in_16,
  input  in_17,
  output out_18,
  output out_19,
  output out_20,
  output out_21,
  output out_22,
  output out_23,
  output out_24,
  output out_25,
  output out_26
);

  wire xor_1_out, xor_2_out, xor_3_out, xor_4_out, xor_5_out, xor_6_out, xor_7_out, xor_8_out;

  ripple_carry_adder ripple_carry_adder_1 (
    .out_23(out_23), .out_24(out_24), .out_25(out_25), .out_26(out_26), .out_18(out_18), .out_19(out_19),
    .out_20(out_20), .out_21(out_21), .out_22(out_22), .in_14(in_16), .in_15(xor_7_out), .in_16(in_17),
    .in_17(xor_8_out), .in_1(in_1), .in_2(xor_1_out), .in_3(in_13), .in_4(in_2), .in_5(xor_2_out),
    .in_6(in_3), .in_7(xor_3_out), .in_8(in_12), .in_9(xor_5_out), .in_10(in_14), .in_11(xor_4_out),
    .in_12(in_15), .in_13(xor_6_out));
  xor xor_1 (xor_1_out, in_4, in_13);
  xor xor_2 (xor_2_out, in_5, in_13);
  xor xor_3 (xor_3_out, in_6, in_13);
  xor xor_4 (xor_4_out, in_8, in_13);
  xor xor_5 (xor_5_out, in_7, in_13);
  xor xor_6 (xor_6_out, in_9, in_13);
  xor xor_7 (xor_7_out, in_10, in_13);
  xor xor_8 (xor_8_out, in_11, in_13);
endmodule
