// Logisim project modular_sap_control.circ as structural Verilog: 11 circuits, main circuit main
module main (
  input  in_1,
  input  in_2,
  input  in_3,
  input  in_4,
  input  in_5,
  input  in_6,
  input  in_7,
  input  in_8,
  input  in_9,
  input  in_10,
  input  in_11,
  input  in_12,
  input  in_13,
  input  in_14,
  input  in_15,
  input  in_16,
  input  in_17,
  input  [7:0] in_18,
  output [3:0] out_19,
  output [7:0] out_20,
  output [7:0] out_21,
  output [7:0] out_22,
  output [7:0] out_23,
  output [7:0] out_24,
  output [7:0] out_25,
  output [7:0] out_26,
  output [7:0] out_27,
  output [7:0] out_28,
  output [7:0] out_29,
  output [7:0] out_30,
  output [7:0] out_31,
  output [7:0] out_32,
  output [7:0] out_33,
  output [7:0] out_34,
  output [7:0] out_35,
  output [7:0] out_36,
  output [3:0] out_37,
  output [3:0] out_38,
  output [7:0] out_39
);

  wire [7:0] reg_gp_1_reg_int_out;

  pc pc_1 (.pc_en(in_13), .pc_clk(in_16), .pc_reset(in_15), .pc_out_en(in_14), .pc_value(out_19), .pc_out(out_37));
  // sram sram_1: pin names not known; wires that end beside it: {out_39[7:4], out_37}, in_8, in_9, {out_39[7:4], out_37}, in_7, in_16, in_12, {out_39[7:4], out_37}, out_21, out_22, out_23, out_24, out_25, out_26, out_27, out_28, out_29, out_30, out_31, out_32, out_33, out_34, out_35, out_36
  assign {out_39[7:4], out_37} = in_17 ? in_18 : 8'bz;  // Controlled_Buffer controlled_buffer_1
  reg_gp reg_gp_1 (
    .reg_in({out_39[7:4], out_37}), .reg_in_en(in_3), .reg_clk(in_16), .reg_out_en(in_4),
    .reg_int_out(reg_gp_1_reg_int_out), .reg_out({out_39[7:4], out_37}));
  reg_gp reg_gp_2 (
    .reg_in({out_39[7:4], out_37}), .reg_in_en(in_1), .reg_clk(in_16), .reg_out_en(in_2),
    .reg_int_out(out_20), .reg_out({out_39[7:4], out_37}));
  ins_reg ins_reg_1 (
    .ins_reg_in({out_39[7:4], out_37}), .ins_reg_in_en(in_10), .clk(in_16), .ins_reg_out_en(in_11),
    .add_outs(out_37), .ins_out(out_38));
  alu alu_1 (
    .alu_in_1(out_20), .alu_out_en(in_5), .alu_sub(in_6), .alu_in_2(reg_gp_1_reg_int_out),
    .alu_out({out_39[7:4], out_37}));  // open: alu_carry_out

  assign out_39[3:0] = out_37;

  // Other names for the same wires on the sheet: a_in = in_1; a_out = in_2; alu_out = in_5; alu_sub = in_6;
  //   b_in = in_3; b_out = in_4; clk = in_16; debug = in_17; debug_data[7:0] = in_18; ins_reg_in_en = in_10;
  //   ins_reg_out_en = in_11; mar_in_en = in_7; pc_en = in_13; pc_out = in_14; pc_reset = in_15; sram_rd = in_8;
  //   sram_wr = in_9

  // Notes on the sheet:
  //   Register A Control
  //   Register B Control
  //   ALU Control
  //   RAM Control
  //   IR Control
  //   PC Control
  //   Debug & Testing
endmodule

module reg_gp (
  input  [7:0] reg_in,
  input  reg_in_en,
  input  reg_clk,
  input  reg_out_en,
  output [7:0] reg_int_out,
  output [7:0] reg_out
);

  wire multiplexer_1_out, multiplexer_2_out, multiplexer_3_out, multiplexer_4_out, multiplexer_5_out,
       multiplexer_6_out, multiplexer_7_out, multiplexer_8_out;

  Multiplexer multiplexer_1 (.in0(reg_int_out[7]), .in1(reg_in[7]), .out(multiplexer_1_out), .sel(reg_in_en));
  D_Flip_Flop d_ff_1 (.D(multiplexer_1_out), .clk(reg_clk), .Q(reg_int_out[7]));  // open: Qn, preset, reset
  assign reg_out[7] = reg_out_en ? reg_int_out[7] : 1'bz;  // Controlled_Buffer controlled_buffer_1
  Multiplexer multiplexer_2 (.in0(reg_int_out[6]), .in1(reg_in[6]), .out(multiplexer_2_out), .sel(reg_in_en));
  D_Flip_Flop d_ff_2 (.D(multiplexer_2_out), .clk(reg_clk), .Q(reg_int_out[6]));  // open: Qn, preset, reset
  Multiplexer multiplexer_3 (.in0(reg_int_out[5]), .in1(reg_in[5]), .out(multiplexer_3_out), .sel(reg_in_en));
  assign reg_out[6] = reg_out_en ? reg_int_out[6] : 1'bz;  // Controlled_Buffer controlled_buffer_2
  D_Flip_Flop d_ff_3 (.D(multiplexer_3_out), .clk(reg_clk), .Q(reg_int_out[5]));  // open: Qn, preset, reset
  Multiplexer multiplexer_4 (.in0(reg_int_out[4]), .in1(reg_in[4]), .out(multiplexer_4_out), .sel(reg_in_en));
  assign reg_out[5] = reg_out_en ? reg_int_out[5] : 1'bz;  // Controlled_Buffer controlled_buffer_3
  D_Flip_Flop d_ff_4 (.D(multiplexer_4_out), .clk(reg_clk), .Q(reg_int_out[4]));  // open: Qn, preset, reset
  Multiplexer multiplexer_5 (.in0(reg_int_out[3]), .in1(reg_in[3]), .out(multiplexer_5_out), .sel(reg_in_en));
  assign reg_out[4] = reg_out_en ? reg_int_out[4] : 1'bz;  // Controlled_Buffer controlled_buffer_4
  D_Flip_Flop d_ff_5 (.D(multiplexer_5_out), .clk(reg_clk), .Q(reg_int_out[3]));  // open: Qn, preset, reset
  Multiplexer multiplexer_6 (.in0(reg_int_out[2]), .in1(reg_in[2]), .out(multiplexer_6_out), .sel(reg_in_en));
  D_Flip_Flop d_ff_6 (.D(multiplexer_6_out), .clk(reg_clk), .Q(reg_int_out[2]));  // open: Qn, preset, reset
  assign reg_out[3] = reg_out_en ? reg_int_out[3] : 1'bz;  // Controlled_Buffer controlled_buffer_5
  assign reg_out[2] = reg_out_en ? reg_int_out[2] : 1'bz;  // Controlled_Buffer controlled_buffer_6
  Multiplexer multiplexer_7 (.in0(reg_int_out[1]), .in1(reg_in[1]), .out(multiplexer_7_out), .sel(reg_in_en));
  D_Flip_Flop d_ff_7 (.D(multiplexer_7_out), .clk(reg_clk), .Q(reg_int_out[1]));  // open: Qn, preset, reset
  assign reg_out[1] = reg_out_en ? reg_int_out[1] : 1'bz;  // Controlled_Buffer controlled_buffer_7
  Multiplexer multiplexer_8 (.in0(reg_int_out[0]), .in1(reg_in[0]), .out(multiplexer_8_out), .sel(reg_in_en));
  D_Flip_Flop d_ff_8 (.D(multiplexer_8_out), .clk(reg_clk), .Q(reg_int_out[0]));  // open: Qn, preset, reset
  assign reg_out[0] = reg_out_en ? reg_int_out[0] : 1'bz;  // Controlled_Buffer controlled_buffer_8

  // Notes on the sheet:
  //   Input
  //   Input Control
  //   Clock
  //   Output Control
  //   Memory
  //   Internal Output
  //   Output
endmodule

module alu (
  input  [7:0] alu_in_1,
  input  alu_out_en,
  input  alu_sub,
  input  [7:0] alu_in_2,
  output alu_carry_out,
  output [7:0] alu_out
);

  wire adder_2_cout, adder_3_cout, adder_4_cout, adder_5_cout, adder_6_cout, adder_7_cout, adder_8_cout,
       xor_1_out, xor_2_out, xor_3_out, xor_4_out, xor_5_out, xor_6_out, xor_7_out, xor_8_out;
  wire [7:0] adder_8_out;

  Adder #(.width(1)) adder_1 (
    .a(alu_in_1[7]), .b(xor_1_out), .out(adder_8_out[7]), .cin(adder_2_cout), .cout(alu_carry_out));
  xor xor_1 (xor_1_out, alu_in_2[7], alu_sub);
  Adder #(.width(1)) adder_2 (
    .a(alu_in_1[6]), .b(xor_2_out), .out(adder_8_out[6]), .cin(adder_3_cout), .cout(adder_2_cout));
  xor xor_2 (xor_2_out, alu_in_2[6], alu_sub);
  Adder #(.width(1)) adder_3 (
    .a(alu_in_1[5]), .b(xor_3_out), .out(adder_8_out[5]), .cin(adder_4_cout), .cout(adder_3_cout));
  xor xor_3 (xor_3_out, alu_in_2[5], alu_sub);
  Adder #(.width(1)) adder_4 (
    .a(alu_in_1[4]), .b(xor_4_out), .out(adder_8_out[4]), .cin(adder_5_cout), .cout(adder_4_cout));
  xor xor_4 (xor_4_out, alu_in_2[4], alu_sub);
  Adder #(.width(1)) adder_5 (
    .a(alu_in_1[3]), .b(xor_5_out), .out(adder_8_out[3]), .cin(adder_6_cout), .cout(adder_5_cout));
  xor xor_5 (xor_5_out, alu_in_2[3], alu_sub);
  Adder #(.width(1)) adder_6 (
    .a(alu_in_1[2]), .b(xor_6_out), .out(adder_8_out[2]), .cin(adder_7_cout), .cout(adder_6_cout));
  xor xor_6 (xor_6_out, alu_in_2[2], alu_sub);
  Adder #(.width(1)) adder_7 (
    .a(alu_in_1[1]), .b(xor_7_out), .out(adder_8_out[1]), .cin(adder_8_cout), .cout(adder_7_cout));
  xor xor_7 (xor_7_out, alu_in_2[1], alu_sub);
  Adder #(.width(1)) adder_8 (.a(alu_in_1[0]), .b(xor_8_out), .out(adder_8_out[0]), .cin(alu_sub), .cout(adder_8_cout));
  xor xor_8 (xor_8_out, alu_in_2[0], alu_sub);
  assign alu_out = alu_out_en ? adder_8_out : 8'bz;  // Controlled_Buffer controlled_buffer_1

  // Notes on the sheet:
  //   Input 1
  //   Carry Output
  //   Subtract Control
  //   Full Adders
  //   Input 2
  //   Output Control
  //   ALU Output
endmodule

module pc (
  input  pc_en,
  input  pc_clk,
  input  pc_reset,
  input  pc_out_en,
  output [3:0] pc_value,
  output [3:0] pc_out
);

  wire j_k_ff_2_qn, j_k_ff_3_qn, j_k_ff_4_qn;

  J_K_Flip_Flop j_k_ff_1 (
    .J(pc_en), .K(pc_en), .clk(j_k_ff_2_qn), .Q(pc_value[3]), .reset(pc_reset));  // open: Qn, preset
  J_K_Flip_Flop j_k_ff_2 (
    .J(pc_en), .K(pc_en), .clk(j_k_ff_3_qn), .Q(pc_value[2]), .Qn(j_k_ff_2_qn), .reset(pc_reset));  // open: preset
  J_K_Flip_Flop j_k_ff_3 (
    .J(pc_en), .K(pc_en), .clk(j_k_ff_4_qn), .Q(pc_value[1]), .Qn(j_k_ff_3_qn), .reset(pc_reset));  // open: preset
  J_K_Flip_Flop j_k_ff_4 (
    .J(pc_en), .K(pc_en), .clk(pc_clk), .Q(pc_value[0]), .Qn(j_k_ff_4_qn), .reset(pc_reset));  // open: preset
  assign pc_out = pc_out_en ? pc_value : 4'bz;  // Controlled_Buffer controlled_buffer_1

  // Notes on the sheet:
  //   Clock
  //   Reset
  //   Output Control
  //   Count Control
  //   Counter Output
endmodule

module dec_4x16 (
  input  [3:0] dec_sel,
  output [15:0] dec_out
);

  wire not_1_out, not_2_out, not_3_out, not_4_out;

  not not_1 (not_1_out, dec_sel[3]);
  not not_2 (not_2_out, dec_sel[2]);
  not not_3 (not_3_out, dec_sel[1]);
  not not_4 (not_4_out, dec_sel[0]);
  and and_1 (dec_out[0], not_4_out, not_3_out, not_2_out, not_1_out);
  and and_2 (dec_out[1], dec_sel[0], not_3_out, not_2_out, not_1_out);
  and and_3 (dec_out[2], not_4_out, dec_sel[1], not_2_out, not_1_out);
  and and_4 (dec_out[3], dec_sel[0], dec_sel[1], not_2_out, not_1_out);
  and and_5 (dec_out[4], not_4_out, not_3_out, dec_sel[2], not_1_out);
  and and_6 (dec_out[5], dec_sel[0], not_3_out, dec_sel[2], not_1_out);
  and and_7 (dec_out[6], not_4_out, dec_sel[1], dec_sel[2], not_1_out);
  and and_8 (dec_out[7], dec_sel[0], dec_sel[1], dec_sel[2], not_1_out);
  and and_9 (dec_out[8], not_4_out, not_3_out, not_2_out, dec_sel[3]);
  and and_10 (dec_out[9], dec_sel[0], not_3_out, not_2_out, dec_sel[3]);
  and and_11 (dec_out[10], not_4_out, dec_sel[1], not_2_out, dec_sel[3]);
  and and_12 (dec_out[11], dec_sel[0], dec_sel[1], not_2_out, dec_sel[3]);
  and and_13 (dec_out[12], not_4_out, not_3_out, dec_sel[2], dec_sel[3]);
  and and_14 (dec_out[13], dec_sel[0], not_3_out, dec_sel[2], dec_sel[3]);
  and and_15 (dec_out[14], not_4_out, dec_sel[1], dec_sel[2], dec_sel[3]);
  and and_16 (dec_out[15], dec_sel[0], dec_sel[1], dec_sel[2], dec_sel[3]);
endmodule

module sram_cell (
  input  [7:0] data_in,
  input  wr_en,
  input  clk,
  input  cs,
  input  rd_en,
  output [7:0] memory_content,
  output [7:0] data_out
);

  wire and_1_out, and_2_out;

  and and_1 (and_1_out, wr_en, cs);
  and and_2 (and_2_out, cs, rd_en);
  reg_gp reg_gp_1 (
    .reg_in(data_in), .reg_in_en(and_1_out), .reg_clk(clk), .reg_out_en(and_2_out),
    .reg_int_out(memory_content), .reg_out(data_out));
endmodule

module sram (
  input  [7:0] sram_d_in,
  input  ram_auto_load,
  input  sram_wr,
  input  sram_rd,
  input  [7:0] mar_d_in,
  input  mar_in_en,
  input  sram_clk,
  output [7:0] sram_d_out,
  output [7:0] out_9,
  output [7:0] out_10,
  output [7:0] out_11,
  output [7:0] out_12,
  output [7:0] out_13,
  output [7:0] out_14,
  output [7:0] out_15,
  output [7:0] out_16,
  output [7:0] out_17,
  output [7:0] out_18,
  output [7:0] out_19,
  output [7:0] out_20,
  output [7:0] out_21,
  output [7:0] out_22,
  output [7:0] out_23,
  output [7:0] out_24
);

  wire multiplexer_2_out;
  wire [3:0] multiplexer_1_out, pc_1_pc_out;
  wire [7:0] controlled_buffer_1_out, controlled_buffer_2_out, multiplexer_3_out, reg_gp_1_reg_int_out,
       rom_1_data;
  wire [15:0] dec_4x16_1_dec_out;

  reg_gp reg_gp_1 (
    .reg_in(mar_d_in), .reg_in_en(mar_in_en), .reg_clk(sram_clk), .reg_int_out(reg_gp_1_reg_int_out));  // open: reg_out_en, reg_out
  pc pc_1 (
    .pc_en(ram_auto_load), .pc_clk(sram_clk), .pc_out_en(ram_auto_load), .pc_out(pc_1_pc_out));  // open: pc_reset, pc_value
  Multiplexer #(.width(4)) multiplexer_1 (
    .in0(reg_gp_1_reg_int_out[3:0]), .in1(pc_1_pc_out), .out(multiplexer_1_out), .sel(ram_auto_load));
  ROM #(.addrWidth(4)) rom_1 (.addr(pc_1_pc_out), .data(rom_1_data));
  dec_4x16 dec_4x16_1 (.dec_sel(multiplexer_1_out), .dec_out(dec_4x16_1_dec_out));
  assign controlled_buffer_1_out = ram_auto_load ? rom_1_data : 8'bz;  // Controlled_Buffer controlled_buffer_1
  Multiplexer multiplexer_2 (.in0(sram_wr), .in1(ram_auto_load), .out(multiplexer_2_out), .sel(ram_auto_load));
  assign controlled_buffer_2_out = multiplexer_2_out ? sram_d_in : 8'bz;  // Controlled_Buffer controlled_buffer_2
  Multiplexer #(.width(8)) multiplexer_3 (
    .in0(controlled_buffer_2_out), .in1(controlled_buffer_1_out), .out(multiplexer_3_out), .sel(ram_auto_load));
  assign sram_d_out = sram_rd ? multiplexer_3_out : 8'bz;  // Controlled_Buffer controlled_buffer_3
  sram_cell sram_cell_1 (
    .data_in(multiplexer_3_out), .wr_en(multiplexer_2_out), .clk(sram_clk), .cs(dec_4x16_1_dec_out[0]),
    .rd_en(sram_rd), .memory_content(out_9), .data_out(multiplexer_3_out));
  sram_cell sram_cell_2 (
    .data_in(multiplexer_3_out), .wr_en(multiplexer_2_out), .clk(sram_clk), .cs(dec_4x16_1_dec_out[1]),
    .rd_en(sram_rd), .memory_content(out_10), .data_out(multiplexer_3_out));
  sram_cell sram_cell_3 (
    .data_in(multiplexer_3_out), .wr_en(multiplexer_2_out), .clk(sram_clk), .cs(dec_4x16_1_dec_out[2]),
    .rd_en(sram_rd), .memory_content(out_11), .data_out(multiplexer_3_out));
  sram_cell sram_cell_4 (
    .data_in(multiplexer_3_out), .wr_en(multiplexer_2_out), .clk(sram_clk), .cs(dec_4x16_1_dec_out[3]),
    .rd_en(sram_rd), .memory_content(out_12), .data_out(multiplexer_3_out));
  sram_cell sram_cell_5 (
    .data_in(multiplexer_3_out), .wr_en(multiplexer_2_out), .clk(sram_clk), .cs(dec_4x16_1_dec_out[4]),
    .rd_en(sram_rd), .memory_content(out_13), .data_out(multiplexer_3_out));
  sram_cell sram_cell_6 (
    .data_in(multiplexer_3_out), .wr_en(multiplexer_2_out), .clk(sram_clk), .cs(dec_4x16_1_dec_out[5]),
    .rd_en(sram_rd), .memory_content(out_14), .data_out(multiplexer_3_out));
  sram_cell sram_cell_7 (
    .data_in(multiplexer_3_out), .wr_en(multiplexer_2_out), .clk(sram_clk), .cs(dec_4x16_1_dec_out[6]),
    .rd_en(sram_rd), .memory_content(out_15), .data_out(multiplexer_3_out));
  sram_cell sram_cell_8 (
    .data_in(multiplexer_3_out), .wr_en(multiplexer_2_out), .clk(sram_clk), .cs(dec_4x16_1_dec_out[7]),
    .rd_en(sram_rd), .memory_content(out_16), .data_out(multiplexer_3_out));
  sram_cell sram_cell_9 (
    .data_in(multiplexer_3_out), .wr_en(multiplexer_2_out), .clk(sram_clk), .cs(dec_4x16_1_dec_out[8]),
    .rd_en(sram_rd), .memory_content(out_17), .data_out(multiplexer_3_out));
  sram_cell sram_cell_10 (
    .data_in(multiplexer_3_out), .wr_en(multiplexer_2_out), .clk(sram_clk), .cs(dec_4x16_1_dec_out[9]),
    .rd_en(sram_rd), .memory_content(out_18), .data_out(multiplexer_3_out));
  sram_cell sram_cell_11 (
    .data_in(multiplexer_3_out), .wr_en(multiplexer_2_out), .clk(sram_clk), .cs(dec_4x16_1_dec_out[10]),
    .rd_en(sram_rd), .memory_content(out_19), .data_out(multiplexer_3_out));
  sram_cell sram_cell_12 (
    .data_in(multiplexer_3_out), .wr_en(multiplexer_2_out), .clk(sram_clk), .cs(dec_4x16_1_dec_out[11]),
    .rd_en(sram_rd), .memory_content(out_20), .data_out(multiplexer_3_out));
  sram_cell sram_cell_13 (
    .data_in(multiplexer_3_out), .wr_en(multiplexer_2_out), .clk(sram_clk), .cs(dec_4x16_1_dec_out[12]),
    .rd_en(sram_rd), .memory_content(out_21), .data_out(multiplexer_3_out));
  sram_cell sram_cell_14 (
    .data_in(multiplexer_3_out), .wr_en(multiplexer_2_out), .clk(sram_clk), .cs(dec_4x16_1_dec_out[13]),
    .rd_en(sram_rd), .memory_content(out_22), .data_out(multiplexer_3_out));
  sram_cell sram_cell_15 (
    .data_in(multiplexer_3_out), .wr_en(multiplexer_2_out), .clk(sram_clk), .cs(dec_4x16_1_dec_out[14]),
    .rd_en(sram_rd), .memory_content(out_23), .data_out(multiplexer_3_out));
  sram_cell sram_cell_16 (
    .data_in(multiplexer_3_out), .wr_en(multiplexer_2_out), .clk(sram_clk), .cs(dec_4x16_1_dec_out[15]),
    .rd_en(sram_rd), .memory_content(out_24), .data_out(multiplexer_3_out));

  // Notes on the sheet:
  //   contents of rom_1 (hex, n*v repeats v):
  //   1 2 3 4 5 6 7 8 9 10 11 12 13 14 15 16
endmodule

module testt (
  input  in_1,
  input  in_2,
  input  in_3,
  input  in_4,
  output [3:0] out_5
);

  pc pc_1 (.pc_en(in_1), .pc_clk(in_2), .pc_reset(in_3), .pc_out_en(in_4), .pc_value(out_5));  // open: pc_out
endmodule

module ins_reg (
  input  [7:0] ins_reg_in,
  input  ins_reg_in_en,
  input  clk,
  input  ins_reg_out_en,
  output [3:0] add_outs,
  output [3:0] ins_out
);

  wire [3:0] reg_gp_1_reg_int_out;

  reg_gp reg_gp_1 (
    .reg_in(ins_reg_in), .reg_in_en(ins_reg_in_en), .reg_clk(clk),
    .reg_int_out({ins_out, reg_gp_1_reg_int_out}));  // open: reg_out_en, reg_out
  assign add_outs = ins_reg_out_en ? reg_gp_1_reg_int_out : 4'bz;  // Controlled_Buffer controlled_buffer_1
endmodule

module ring_counter (
  input  clk,
  input  ring_reset,
  output [7:0] count_out
);

  wire controlled_buffer_1_out, not_1_out, pull_resistor_1_node;
  wire [3:0] pc_1_pc_value;
  wire [15:8] dec_4x16_1_dec_out;

  assign controlled_buffer_1_out = ring_reset ? ring_reset : 1'bz;  // Controlled_Buffer controlled_buffer_1
  not not_1 (not_1_out, ring_reset);
  Pull_Resistor #(.pull(1)) pull_resistor_1 (.node(pull_resistor_1_node));
  assign controlled_buffer_1_out = not_1_out ? count_out[6] : 1'bz;  // Controlled_Buffer controlled_buffer_2
  pc pc_1 (
    .pc_en(pull_resistor_1_node), .pc_clk(clk), .pc_reset(controlled_buffer_1_out),
    .pc_out_en(pull_resistor_1_node), .pc_value(pc_1_pc_value));  // open: pc_out
  dec_4x16 dec_4x16_1 (.dec_sel(pc_1_pc_value), .dec_out({dec_4x16_1_dec_out, count_out}));
endmodule

module cs (
  input  clk,
  input  reset,
  input  [3:0] ins,
  output pc_out,
  output ins_in,
  output pc_en,
  output ins_out,
  output mar_in,
  output reg_a,
  output ram_rd
);

  wire and_1_out, and_3_out, and_4_out, and_5_out;
  wire [7:0] ring_counter_1_count_out;
  wire [15:0] dec_4x16_1_dec_out;

  dec_4x16 dec_4x16_1 (.dec_sel(ins), .dec_out(dec_4x16_1_dec_out));
  ring_counter ring_counter_1 (
    .clk(clk), .ring_reset(reset),
    .count_out({ring_counter_1_count_out[7:3], pc_en, ring_counter_1_count_out[1:0]}));
  and and_1 (and_1_out, ring_counter_1_count_out[3], dec_4x16_1_dec_out[0]);
  and and_2 (reg_a, ring_counter_1_count_out[4], dec_4x16_1_dec_out[0]);
  and and_3 (and_3_out, ring_counter_1_count_out[0], dec_4x16_1_dec_out[0]);
  or or_1 (mar_in, and_1_out, and_3_out);
  and and_4 (and_4_out, ring_counter_1_count_out[1], dec_4x16_1_dec_out[0]);
  or or_2 (ram_rd, and_4_out, and_5_out);
  and and_5 (and_5_out, ring_counter_1_count_out[4], dec_4x16_1_dec_out[0]);
  and and_6 (pc_out, ring_counter_1_count_out[0], dec_4x16_1_dec_out[0]);
  and and_7 (ins_in, ring_counter_1_count_out[1], dec_4x16_1_dec_out[0]);
  and and_8 (ins_out, dec_4x16_1_dec_out[0], ring_counter_1_count_out[3]);
endmodule
